# Fritzing sketch ArduinoMini_Photogate_Receiver (saved by Fritzing 0.9.3b)

parts:
  Part1 = Arduino Nano (Rev3.0)
  U2 = LCD-16X2 [package=lcd-16x2]  # not connected
  Part2 = NRF24L01+ Breakout Board
  J1 = Infrared Proximity Sensor

nets:
  GND: Part1.GND, Part2.GND, J1.GND
  N1: Part1.D9, Part2.CE
  N2: Part1.D10, Part2.CS
  N3: Part1.D11/MOSI, Part2.MOSI
  N4: Part1.D12/MISO, Part2.MISO
  5V: Part1.5V, J1.Vcc
  N5: Part1.A6, J1.Vout
  3V3: Part1.3V3, Part2.VCC
  N6: Part1.D13/SCK, Part2.SCK
