# Fritzing sketch ArduinoMini_Photogate_Transmitter (saved by Fritzing 0.9.3b)
breadboards: 1

parts:
  Part1 = Arduino Nano (Rev3.0)
  J1 = Infrared Proximity Sensor
  Part2 = NRF24L01+ Breakout Board
  S1 = Toggle Switch [package=THT]
  S2 = Pushbutton [package="[THT]"]
  R1 = Resistor [tolerance=±5% resistance=220 package="1206 [SMD]"]
  BAT1 = BC9VPC [package=bc9vpc]

nets:
  GND: Part1.GND, J1.GND, Part2.GND, S1.COM, R1.Pin_0, BAT1.V+
  3V3: Part1.D7, Part1.3V3, Part2.VCC, S2.Pin_3, S2.Pin_4, R1.Pin_1
  N1: Part1.D9, Part2.CE
  N2: Part1.D10, Part2.CS
  N3: Part1.D11/MOSI, Part2.MOSI
  N4: Part1.D12/MISO, Part2.MISO
  N5: Part1.VIN, S1.L1, BAT1.V-
  5V: Part1.5V, J1.Vcc
  N6: Part1.A6, J1.Vout
  N7: Part1.D13/SCK, Part2.SCK
  N8: S2.Pin_1, S2.Pin_2
